// Logisim project praktik_1.2.circ as structural Verilog: 1 circuit, main circuit main
module main (
  input  A,
  input  B,
  output Y
);

  and and_1 (Y, A, B);
  LED led_1 (.in(Y));

  // Notes on the sheet:
  //   Modul Praktikum 2
endmodule
